# Fritzing sketch Fenix (saved by Fritzing 0.9.3b)
breadboards: 1

parts:
  Arduino2 = Arduino Mega 2560 (Rev3)
  Componente4 = MD10C R2
  M2 = DC Motor
  R2 = Rotary Potentiometer (Small) [maximum_resistance=100kΩ package=THT]
  Componente5 = 9-DOF Absolute Orientation IMU Fusion Breakout - BNO055
  J1 = Piezo Speaker
  Componente6 = Bluetooth HC-05 Macho
  R3 = Resistor [tolerance=±5% resistance=2.2k package=THT]
  R4 = Resistor [tolerance=±5% resistance=1k package=THT]

nets:
  N1: Arduino2.A8, R2.wiper
  N2: Arduino2.D21/SCL, Componente5.SCL_5V
  N3: Arduino2.D20/SDA, Componente5.SDA_5V
  N4: Arduino2.D19/RX1, Componente6.TXD
  N5: Arduino2.D18/TX1, R4.Pin_0
  GND: Arduino2.GND, Componente4.no_name_yet#connector_3, R2.leg2, Componente5.GND, J1.pin1, Componente6.GND, R3.Pin_1
  N6: Arduino2.D8_PWM, J1.pin2
  5V: Arduino2.5V, R2.leg1, Componente5.5.0V, Componente5.3.3V
  N7: Arduino2.D6_PWM, Componente4.no_name_yet#connector_2
  N8: Arduino2.D7_PWM, Componente4.no_name_yet#connector_1
  N9: Componente4.no_name_yet#connectorA-3, M2.pin_2
  N10: Componente4.no_name_yet#connectorB-4, M2.pin_1
  N11: Componente6.RXD, R3.Pin_0, R4.Pin_1

custom parts:
  9-DOF Absolute Orientation IMU Fusion Breakout - BNO055: A MEMS accelerometer, magnetometer and gyroscope on a single die with a high speed ARM Cortex-M0 based processor to digest all the sensor data, abstract the sensor fusion and real time requirements away, and spit out data you can use in quaternions, Euler angles or vectors.
